// Logisim project sprout8.circ as structural Verilog: 4 circuits, main circuit main
module main (
);

  reg8 reg8_1 ();  // open: d, load, clk, reset_value, rst, q
  pc pc_1 ();  // open: d, load, inc, clk, rst, q
  ir ir_1 ();  // open: d, load0, clk, rst, load1, ir0, rs, rd, opcode, ir1
endmodule

module pc (
  input  [7:0] d,
  input  load,
  input  inc,
  input  clk,
  input  rst,
  output [7:0] q
);

  wire or_1_out;
  wire [7:0] adder_1_out, multiplexer_1_out;

  Multiplexer #(.width(8)) multiplexer_1 (.in0(adder_1_out), .in1(d), .out(multiplexer_1_out), .sel(load));
  or or_1 (or_1_out, load, inc);
  Register register_1 (.D(multiplexer_1_out), .en(or_1_out), .clk(clk), .Q(q), .clr(rst));
  Adder adder_1 (.a(8'h1), .b(q), .out(adder_1_out));  // open: cin, cout

  // Notes on the sheet:
  //   PROGRAM COUNTER CIRCUIT (PROGRAM COUNTER)
endmodule

module reg8 (
  input  [7:0] d,
  input  load,
  input  clk,
  input  [7:0] reset_value,
  input  rst,
  output [7:0] q
);

  wire [7:0] register_1_q;

  Register register_1 (.D(d), .en(load), .clk(clk), .Q(register_1_q), .clr(rst));
  Multiplexer #(.width(8)) multiplexer_1 (.in0(register_1_q), .in1(reset_value), .out(q), .sel(rst));

  // Notes on the sheet:
  //   MEMORY ADDRESS REGISTER (MAR/REG8)
endmodule

module ir (
  input  [7:0] d,
  input  load0,
  input  clk,
  input  rst,
  input  load1,
  output [7:0] ir0,
  output [1:0] rs,
  output [1:0] rd,
  output [3:0] opcode,
  output [7:0] ir1
);

  Register register_1 (.D(d), .en(load0), .clk(clk), .Q(ir0), .clr(rst));
  Register register_2 (.D(d), .en(load1), .clk(clk), .Q(ir1), .clr(rst));

  assign opcode = ir0[7:4];
  assign rd = ir0[3:2];
  assign rs = ir0[1:0];

  // Notes on the sheet:
  //   INSTRUCTION REGISTER (IR)
endmodule
